// Logisim project 0to9automaticCounterWithDisplay.circ as structural Verilog: 1 circuit, main circuit main
module main (
);

  wire a_out, and_1_out, and_2_out, and_3_out, and_4_out, and_5_out, and_6_out, and_7_out, and_8_out,
       and_9_out, b_out, buffer_1_out, buffer_2_out, buffer_3_out, buffer_4_out, buffer_5_out, buffer_6_out,
       buffer_7_out, buffer_8_out, buffer_9_out, buffer_10_out, c_out, clock_1_out, clock_2_out, clock_3_out,
       clock_4_out, clock_5_out, clock_6_out, clock_7_out, clock_8_out, clock_9_out, clock_10_out, d_out,
       e_out, f_out, g_out, not_1_out, not_2_out, not_3_out, not_4_out, not_5_out, not_6_out, not_7_out,
       not_8_out, not_9_out;

  Clock #(.highDuration(10)) clock_1 (.out(clock_1_out));
  Clock #(.highDuration(9), .lowDuration(2)) clock_2 (.out(clock_2_out));
  Clock #(.highDuration(8), .lowDuration(3)) clock_3 (.out(clock_3_out));
  Clock #(.highDuration(7), .lowDuration(4)) clock_4 (.out(clock_4_out));
  Clock #(.highDuration(6), .lowDuration(5)) clock_5 (.out(clock_5_out));
  Clock #(.highDuration(5), .lowDuration(6)) clock_6 (.out(clock_6_out));
  Clock #(.highDuration(4), .lowDuration(7)) clock_7 (.out(clock_7_out));
  Clock #(.highDuration(3), .lowDuration(8)) clock_8 (.out(clock_8_out));
  Clock #(.highDuration(2), .lowDuration(9)) clock_9 (.out(clock_9_out));
  Clock #(.lowDuration(10)) clock_10 (.out(clock_10_out));
  and and_1 (and_1_out, clock_1_out, not_1_out);
  not not_1 (not_1_out, clock_2_out);
  not not_2 (not_2_out, clock_3_out);
  not not_3 (not_3_out, clock_4_out);
  not not_4 (not_4_out, clock_5_out);
  not not_5 (not_5_out, clock_6_out);
  not not_6 (not_6_out, clock_7_out);
  not not_7 (not_7_out, clock_8_out);
  not not_8 (not_8_out, clock_9_out);
  not not_9 (not_9_out, clock_10_out);
  and and_2 (and_2_out, clock_2_out, not_2_out);
  and and_3 (and_3_out, clock_3_out, not_3_out);
  and and_4 (and_4_out, clock_4_out, not_4_out);
  and and_5 (and_5_out, clock_5_out, not_5_out);
  and and_6 (and_6_out, clock_6_out, not_6_out);
  and and_7 (and_7_out, clock_7_out, not_7_out);
  and and_8 (and_8_out, clock_8_out, not_8_out);
  and and_9 (and_9_out, clock_9_out, not_9_out);
  buf buffer_1 (buffer_1_out, and_1_out);
  buf buffer_2 (buffer_2_out, and_2_out);
  buf buffer_3 (buffer_3_out, and_3_out);
  buf buffer_4 (buffer_4_out, and_4_out);
  buf buffer_5 (buffer_5_out, and_5_out);
  buf buffer_6 (buffer_6_out, and_6_out);
  buf buffer_7 (buffer_7_out, and_7_out);
  buf buffer_8 (buffer_8_out, and_8_out);
  buf buffer_9 (buffer_9_out, and_9_out);
  buf buffer_10 (buffer_10_out, clock_10_out);
  or a (a_out, buffer_1_out, buffer_3_out, buffer_4_out, buffer_6_out, buffer_7_out, buffer_8_out, buffer_9_out, buffer_10_out);
  or b (b_out, buffer_6_out, buffer_1_out, buffer_5_out, buffer_7_out, buffer_9_out, buffer_10_out);
  or c (c_out, buffer_1_out, buffer_2_out, buffer_3_out, buffer_4_out, buffer_5_out, buffer_8_out, buffer_9_out, buffer_10_out);
  or d (d_out, buffer_3_out, buffer_4_out, buffer_5_out, buffer_7_out, buffer_9_out, buffer_10_out, buffer_6_out);
  _7_Segment_Display u_7_segment_display_1 (
    .g(d_out), .f(b_out), .a(a_out), .b(c_out), .e(e_out), .d(g_out), .c(f_out));  // open: dp
  or e (e_out, buffer_1_out, buffer_3_out, buffer_9_out, buffer_7_out);
  or f (f_out, buffer_1_out, buffer_2_out, buffer_4_out, buffer_5_out, buffer_6_out, buffer_7_out, buffer_8_out, buffer_9_out, buffer_10_out);
  or g (g_out, buffer_1_out, buffer_3_out, buffer_4_out, buffer_6_out, buffer_7_out, buffer_9_out, buffer_10_out);
endmodule
