// Logisim project 8BitAdder.circ as structural Verilog: 3 circuits, main circuit main
module main (
  input  [7:0] X,
  input  [7:0] in_2,
  output [8:0] out_3
);

  wire fulladder_2_carryout, fulladder_3_carryout, fulladder_4_carryout, fulladder_5_carryout,
       fulladder_6_carryout, fulladder_7_carryout, halfadder_1_carry;

  FullAdder fulladder_1 (.CarryIn(fulladder_2_carryout), .a(in_2[7]), .b(X[7]), .sum(out_3[7]), .CarryOut(out_3[8]));
  LedBar #(.matrixcols(9)) ledbar_1 (
    .led0(out_3[8]), .led1(out_3[7]), .led2(out_3[6]), .led3(out_3[5]), .led4(out_3[4]), .led5(out_3[3]),
    .led6(out_3[2]), .led7(out_3[1]), .led8(out_3[0]));
  FullAdder fulladder_2 (
    .CarryIn(fulladder_3_carryout), .a(in_2[6]), .b(X[6]), .sum(out_3[6]), .CarryOut(fulladder_2_carryout));
  LED led_1 (.in(fulladder_2_carryout));
  FullAdder fulladder_3 (
    .CarryIn(fulladder_4_carryout), .a(in_2[5]), .b(X[5]), .sum(out_3[5]), .CarryOut(fulladder_3_carryout));
  LED led_2 (.in(fulladder_3_carryout));
  LED led_3 (.in(fulladder_4_carryout));
  FullAdder fulladder_4 (
    .CarryIn(fulladder_5_carryout), .a(in_2[4]), .b(X[4]), .sum(out_3[4]), .CarryOut(fulladder_4_carryout));
  FullAdder fulladder_5 (
    .CarryIn(fulladder_6_carryout), .a(in_2[3]), .b(X[3]), .sum(out_3[3]), .CarryOut(fulladder_5_carryout));
  LED led_4 (.in(fulladder_5_carryout));
  FullAdder fulladder_6 (
    .CarryIn(fulladder_7_carryout), .a(in_2[2]), .b(X[2]), .sum(out_3[2]), .CarryOut(fulladder_6_carryout));
  LED led_5 (.in(fulladder_6_carryout));
  FullAdder fulladder_7 (
    .CarryIn(halfadder_1_carry), .a(in_2[1]), .b(X[1]), .sum(out_3[1]), .CarryOut(fulladder_7_carryout));
  LED led_6 (.in(fulladder_7_carryout));
  LED led_7 (.in(halfadder_1_carry));
  HalfAdder halfadder_1 (.a(in_2[0]), .b(X[0]), .sum(out_3[0]), .carry(halfadder_1_carry));
endmodule

module HalfAdder (
  input  a,
  input  b,
  output sum,
  output carry
);

  and and_1 (carry, b, a);
  xor xor_1 (sum, a, b);
endmodule

module FullAdder (
  input  CarryIn,
  input  a,
  input  b,
  output sum,
  output CarryOut
);

  wire and_1_out, and_2_out, xor_1_out;

  xor xor_1 (xor_1_out, a, b);
  and and_1 (and_1_out, b, a);
  xor xor_2 (sum, CarryIn, xor_1_out);
  and and_2 (and_2_out, CarryIn, xor_1_out);
  or or_1 (CarryOut, and_2_out, and_1_out);
endmodule
