// Logisim project BankSecurity.circ as structural Verilog: 1 circuit, main circuit main
module main (
  input  J,
  input  L,
  input  K,
  output X
);

  wire and_1_out;

  and and_1 (and_1_out, J, L);
  and and_2 (X, and_1_out, ~K);  // AND_Gate
endmodule
