// Logisim project Gemstone.circ as structural Verilog: 1 circuit, main circuit main
module main (
  input  J,
  input  K,
  output X
);

  wire not_1_out;

  not not_1 (not_1_out, K);
  or or_1 (X, J, not_1_out);
endmodule
